// Logisim project cpu8_v1.circ as structural Verilog: 8 circuits, main circuit CPU8
module CPU8 (
  input  Clock,
  input  Reset,
  input  [7:0] ValueIn,
  output [7:0] ValueOut
);

  wire and_1_out, cond8_1_valueout, decoder_1_out6, decoder_2_out6, decoder_3_out0, decoder_3_out1,
       decoder_3_out2, decoder_3_out3, decoder_4_out0, decoder_4_out1, decoder_4_out2, decoder_4_out3,
       decoder_4_out4, decoder_4_out5, decoder_5_out0, decoder_5_out1, decoder_5_out2, decoder_5_out3,
       decoder_5_out4, decoder_5_out5, not_1_out, or_1_out, or_2_out, or_3_out;
  wire [7:0] alu8_1_valueout, ConstantLoading_q, GeneralPurposeA_q, GeneralPurposeB_q, OperandA_q,
       OperandB_q, Program_data, ProgramCounter_q, Result_q, transistor_2_out;

  Counter ProgramCounter (
    .clr(Reset), .load(and_1_out), .up(1'b1), .count(not_1_out), .clk(Clock), .D(transistor_2_out),
    .Q(ProgramCounter_q));  // open: carry
  not not_1 (not_1_out, and_1_out);
  ROM Program (.addr(ProgramCounter_q), .data(Program_data));
  // Probe on ValueIn
  // Probe on ValueOut
  // Probe on Program_data
  Pull_Resistor #(.pull(1)) pull_resistor_1 (.node(ValueOut));
  Transistor #(.\type ("n"), .width(8)) transistor_1 (.in(transistor_2_out), .out(ValueOut), .gate(decoder_1_out6));
  Decoder #(.select(3)) decoder_1 (
    .out6(decoder_1_out6), .sel(Program_data[2:0]), .en(decoder_3_out2));  // open: out0, out1, out2, out3, out4, out5, out7
  Decoder #(.select(3)) decoder_2 (
    .out6(decoder_2_out6), .sel(Program_data[5:3]), .en(decoder_3_out2));  // open: out0, out1, out2, out3, out4, out5, out7
  Transistor #(.\type ("n"), .width(8)) transistor_2 (.in(ValueIn), .out(transistor_2_out), .gate(decoder_2_out6));
  Decoder #(.enable("false"), .select(2)) decoder_3 (
    .out0(decoder_3_out0), .out1(decoder_3_out1), .out2(decoder_3_out2), .out3(decoder_3_out3),
    .sel(Program_data[7:6]));
  and and_1 (and_1_out, decoder_3_out3, cond8_1_valueout);
  // Probe on transistor_2_out
  Transistor #(.\type ("n"), .width(8)) transistor_3 (.in(Program_data), .out(transistor_2_out), .gate(decoder_3_out0));
  // Probe on Program_data[5:3]
  // Probe on Program_data[2:0]
  Decoder #(.select(3)) decoder_4 (
    .out0(decoder_4_out0), .out1(decoder_4_out1), .out2(decoder_4_out2), .out3(decoder_4_out3),
    .out4(decoder_4_out4), .out5(decoder_4_out5), .sel(Program_data[2:0]), .en(decoder_3_out2));  // open: out6, out7
  Pull_Resistor #(.pull(1)) pull_resistor_2 (.node(transistor_2_out));
  or or_1 (or_1_out, decoder_4_out0, decoder_3_out0);
  or or_2 (or_2_out, decoder_4_out3, decoder_3_out1);
  Register ConstantLoading (.D(transistor_2_out), .en(or_1_out), .clk(Clock), .Q(ConstantLoading_q), .clr(Reset));
  Register OperandA (.D(transistor_2_out), .en(decoder_4_out1), .clk(Clock), .Q(OperandA_q), .clr(Reset));
  Register OperandB (.D(transistor_2_out), .en(decoder_4_out2), .clk(Clock), .Q(OperandB_q), .clr(Reset));
  Register Result (.D(transistor_2_out), .en(or_2_out), .clk(Clock), .Q(Result_q), .clr(Reset));
  Register GeneralPurposeA (.D(transistor_2_out), .en(decoder_4_out4), .clk(Clock), .Q(GeneralPurposeA_q), .clr(Reset));
  Register GeneralPurposeB (.D(transistor_2_out), .en(decoder_4_out5), .clk(Clock), .Q(GeneralPurposeB_q), .clr(Reset));
  // Probe on OperandA_q
  // Probe on OperandB_q
  // Probe on Result_q
  or or_3 (or_3_out, decoder_3_out3, decoder_5_out0);
  Decoder #(.select(3)) decoder_5 (
    .out0(decoder_5_out0), .out1(decoder_5_out1), .out2(decoder_5_out2), .out3(decoder_5_out3),
    .out4(decoder_5_out4), .out5(decoder_5_out5), .sel(Program_data[5:3]), .en(decoder_3_out2));  // open: out6, out7
  Transistor #(.\type ("n"), .width(8)) transistor_4 (.in(ConstantLoading_q), .out(transistor_2_out), .gate(or_3_out));
  Transistor #(.\type ("n"), .width(8)) transistor_5 (.in(OperandA_q), .out(transistor_2_out), .gate(decoder_5_out1));
  Transistor #(.\type ("n"), .width(8)) transistor_6 (.in(OperandB_q), .out(transistor_2_out), .gate(decoder_5_out2));
  Transistor #(.\type ("n"), .width(8)) transistor_7 (.in(Result_q), .out(transistor_2_out), .gate(decoder_5_out3));
  Transistor #(.\type ("n"), .width(8)) transistor_8 (
    .in(GeneralPurposeA_q), .out(transistor_2_out), .gate(decoder_5_out4));
  Transistor #(.\type ("n"), .width(8)) transistor_9 (
    .in(GeneralPurposeB_q), .out(transistor_2_out), .gate(decoder_5_out5));
  Transistor #(.\type ("n"), .width(8)) transistor_10 (
    .in(alu8_1_valueout), .out(transistor_2_out), .gate(decoder_3_out1));
  ALU8 alu8_1 (.Operand1(OperandA_q), .Operand2(OperandB_q), .OpCode(Program_data[2:0]), .ValueOut(alu8_1_valueout));
  Cond8 cond8_1 (.ValueIn(Result_q), .OpCode(Program_data[2:0]), .ValueOut(cond8_1_valueout));

  // Notes on the sheet:
  //   Op Types:
  //   ALU Ops:
  //   0: And
  //   1: Or
  //   2: Nand
  //   3: Nor
  //   4: Add
  //   5: Subtract
  //   1: ALU [Reg1, Reg2]->[Reg3] - (0:2 ALU Op)
  //   3: Cond [Reg0] - (0:2 Comparison Op)
  //   1: = 0
  //   2: < 0
  //   3: <= 0
  //   5: != 0
  //   6: > 0
  //   7: >= 0
  //   contents of Program (hex, n*v repeats v):
  //   30 86 31 86 32 86 33 86 34 86 35 86 36 86 37 86 38 86 39 86 0 c4
  //   0: Load [Constant]->[Reg0] - (0:5 Constant)
  //   2: Copy [RegA]->[RegB] - (3:5 Source, 0:2 Dest)
  //   Cond Ops:
  //   0: Never
  //   4: Always
  //   6: Output
  //   Constant
  //   Argument 0 (DEST)
  //   Argument 1 (SRC)
  //   Op Type
  //   Jump to Reg0
  //   6: Input
  //   ->
  //   Save Selector
  //   Load Selector
endmodule

module ALU8 (
  input  [7:0] Operand1,
  input  [7:0] Operand2,
  input  [2:0] OpCode,
  output [7:0] ValueOut
);

  wire [7:0] adder_1_out, and_1_out, nand_1_out, nor_1_out, or_1_out, subtractor_1_out;

  Adder adder_1 (.a(Operand2), .b(Operand1), .out(adder_1_out));  // open: cin, cout
  Subtractor subtractor_1 (.a(Operand2), .b(Operand1), .out(subtractor_1_out));  // open: bin, bout
  assign and_1_out = Operand2 & Operand1;  // AND_Gate and_1, 8 bits wide
  assign or_1_out = Operand2 | Operand1;  // OR_Gate or_1, 8 bits wide
  assign nand_1_out = ~(Operand2 & Operand1);  // NAND_Gate nand_1, 8 bits wide
  assign nor_1_out = ~(Operand2 | Operand1);  // NOR_Gate nor_1, 8 bits wide
  Multiplexer #(.select(3), .width(8)) multiplexer_1 (
    .in0(and_1_out), .in1(or_1_out), .in2(nand_1_out), .in3(nor_1_out), .in4(adder_1_out),
    .in5(subtractor_1_out), .out(ValueOut), .sel(OpCode));  // open: in6, in7

  // Notes on the sheet:
  //   1: Or
  //   3: Nor
  //   0: And
  //   2: Nand
  //   4: Add
  //   5: Subtract
endmodule

module HalfAdder (
  input  Addend1,
  input  Addend2,
  output ValueOut,
  output CarryOut
);

  wire not_1_out, or_1_out;

  or or_1 (or_1_out, Addend1, Addend2);
  and and_1 (CarryOut, Addend1, Addend2);
  not not_1 (not_1_out, CarryOut);
  and and_2 (ValueOut, or_1_out, not_1_out);
endmodule

module FullAdder (
  input  Addend1,
  input  Addend2,
  input  CarryIn,
  output ValueOut,
  output CarryOut
);

  wire halfadder_1_carryout, halfadder_1_valueout, halfadder_2_carryout;

  HalfAdder halfadder_1 (
    .Addend1(Addend1), .Addend2(Addend2), .ValueOut(halfadder_1_valueout), .CarryOut(halfadder_1_carryout));
  HalfAdder halfadder_2 (
    .Addend1(halfadder_1_valueout), .Addend2(CarryIn), .ValueOut(ValueOut), .CarryOut(halfadder_2_carryout));
  or or_1 (CarryOut, halfadder_2_carryout, halfadder_1_carryout);
endmodule

module Adder8 (
  input  [7:0] Addend1,
  input  [7:0] Addend2,
  input  CarryIn,
  output [7:0] ValueOut,
  output CarryOut
);

  wire fulladder_1_carryout, fulladder_2_carryout, fulladder_3_carryout, fulladder_4_carryout,
       fulladder_5_carryout, fulladder_6_carryout, fulladder_7_carryout;

  FullAdder fulladder_1 (
    .Addend1(Addend1[0]), .Addend2(Addend2[0]), .CarryIn(CarryIn), .ValueOut(ValueOut[0]),
    .CarryOut(fulladder_1_carryout));
  FullAdder fulladder_2 (
    .Addend1(Addend1[1]), .Addend2(Addend2[1]), .CarryIn(fulladder_1_carryout), .ValueOut(ValueOut[1]),
    .CarryOut(fulladder_2_carryout));
  FullAdder fulladder_3 (
    .Addend1(Addend1[2]), .Addend2(Addend2[2]), .CarryIn(fulladder_2_carryout), .ValueOut(ValueOut[2]),
    .CarryOut(fulladder_3_carryout));
  FullAdder fulladder_4 (
    .Addend1(Addend1[3]), .Addend2(Addend2[3]), .CarryIn(fulladder_3_carryout), .ValueOut(ValueOut[3]),
    .CarryOut(fulladder_4_carryout));
  FullAdder fulladder_5 (
    .Addend1(Addend1[4]), .Addend2(Addend2[4]), .CarryIn(fulladder_4_carryout), .ValueOut(ValueOut[4]),
    .CarryOut(fulladder_5_carryout));
  FullAdder fulladder_6 (
    .Addend1(Addend1[5]), .Addend2(Addend2[5]), .CarryIn(fulladder_5_carryout), .ValueOut(ValueOut[5]),
    .CarryOut(fulladder_6_carryout));
  FullAdder fulladder_7 (
    .Addend1(Addend1[6]), .Addend2(Addend2[6]), .CarryIn(fulladder_6_carryout), .ValueOut(ValueOut[6]),
    .CarryOut(fulladder_7_carryout));
  FullAdder fulladder_8 (
    .Addend1(Addend1[7]), .Addend2(Addend2[7]), .CarryIn(fulladder_7_carryout), .ValueOut(ValueOut[7]),
    .CarryOut(CarryOut));
endmodule

module Cond8 (
  input  [7:0] ValueIn,
  input  [2:0] OpCode,
  output ValueOut
);

  wire not_1_out, not_2_out, not_3_out, or_1_out, zero8_1_valueout;

  Zero8 zero8_1 (.ValueIn(ValueIn), .ValueOut(zero8_1_valueout));
  or or_1 (or_1_out, ValueIn[7], zero8_1_valueout);
  not not_1 (not_1_out, or_1_out);
  not not_2 (not_2_out, zero8_1_valueout);
  not not_3 (not_3_out, ValueIn[7]);
  Multiplexer #(.select(3)) multiplexer_1 (
    .in0(1'b0), .in1(zero8_1_valueout), .in2(ValueIn[7]), .in3(or_1_out), .in4(1'b1), .in5(not_2_out),
    .in6(not_1_out), .in7(not_3_out), .out(ValueOut), .sel(OpCode));

  // Notes on the sheet:
  //   0: Never
  //   1: = 0
  //   2: < 0
  //   3: <= 0
  //   4: Always
  //   5: != 0
  //   6: > 0
  //   7: >= 0
endmodule

module Zero8 (
  input  [7:0] ValueIn,
  output ValueOut
);

  and and_1 (ValueOut, ~ValueIn[0], ~ValueIn[1], ~ValueIn[2], ~ValueIn[3], ~ValueIn[4], ~ValueIn[5], ~ValueIn[6], ~ValueIn[7]);  // AND_Gate
endmodule

module SoC8_TTY (
);

  wire clock_1_out, Reset_out;
  wire [7:0] cpu8_1_valueout;

  Clock clock_1 (.out(clock_1_out));
  Button Reset (.out(Reset_out));
  CPU8 cpu8_1 (.Clock(clock_1_out), .Reset(Reset_out), .ValueOut(cpu8_1_valueout));  // open: ValueIn
  TTY tty_1 (.data(cpu8_1_valueout[6:0]), .clk(clock_1_out), .we(1'b1), .clr(Reset_out));
endmodule
